# Fritzing sketch MqttEsquema (saved by Fritzing 0.9.6b)
breadboards: 1

parts:
  U1 = NodeMCU V3.0
  R1 = Rotary Potentiometer (Large) [maximum_resistance=100kΩ package=THT]
  R2 = Resistor [tolerance=±5% power=0.25 resistance=220 package=THT]
  R3 = Resistor [tolerance=±5% power=0.25 resistance=220 package=THT]
  R4 = Resistor [tolerance=±5% power=0.25 resistance=220 package=THT]
  R5 = Resistor [tolerance=±5% power=0.25 resistance=220 package=THT]
  LED1 = LED - 5mm [color="Red (633nm)" current=0.030 package="5 mm [THT]"]
  LED2 = LED - 5mm [color="Red (633nm)" current=0.030 package="5 mm [THT]"]
  LED3 = LED - 5mm [color="Red (633nm)" current=0.030 package="5 mm [THT]"]
  LED4 = LED - 5mm [color="Red (633nm)" current=0.030 package="5 mm [THT]"]

nets:
  N1: U1.D1, R2.Pin_0
  N2: U1.D2, R3.Pin_0
  N3: U1.D3, R4.Pin_0
  N4: U1.D4, R5.Pin_0
  N5: U1.GND#6, U1.GND#16, LED1.cathode, LED2.cathode, LED3.cathode, LED4.cathode
  N6: U1.GND#41, R1.leg1
  N7: U1.A0, R1.wiper
  N8: R2.Pin_1, LED4.anode
  N9: R3.Pin_1, LED3.anode
  N10: R4.Pin_1, LED2.anode
  N11: R5.Pin_1, LED1.anode

custom parts:
  NodeMCU V3.0: ESP8266 based NodeMCU
