# Fritzing sketch PotenciometroEsquema (saved by Fritzing 0.9.6b)
breadboards: 1

parts:
  U1 = NodeMCU V3.0
  R1 = Rotary Potentiometer (Large) [maximum_resistance=100kΩ package=THT]

nets:
  N1: U1.GND, R1.leg2
  N2: U1.A0, R1.wiper

custom parts:
  NodeMCU V3.0: ESP8266 based NodeMCU
