# Fritzing sketch Diagrama_PCA9685 v2 (saved by Fritzing 0.9.6b)

parts:
  U1 = NodeMCU V3.0
  Componente1 = 16-Channel 12-bit PCA9685 PWM/Servo Driver
  SERVO1 = Tower Pro SG90 servo [part_number=101246]
  SERVO2 = Tower Pro SG90 servo [part_number=101246]
  SERVO3 = Tower Pro SG90 servo [part_number=101246]
  SERVO4 = Tower Pro SG90 servo [part_number=101246]
  SERVO5 = Tower Pro SG90 servo [part_number=101246]
  SERVO6 = Tower Pro SG90 servo [part_number=101246]
  BAT1 = Battery Holders [package=lipo-1100mAh]

nets:
  N1: U1.D1, Componente1.SCL
  N2: U1.D2, Componente1.SDA
  3V3: U1.3V3, Componente1.PWRIN, Componente1.VCC, BAT1.+
  GND: U1.GND, Componente1.GND, SERVO1.GND, SERVO2.GND, SERVO4.GND, SERVO5.GND, SERVO6.GND, BAT1.-
  +5V: U1.Vin, Componente1.V+, SERVO1.+5V, SERVO2.+5V, SERVO3.+5V, SERVO4.+5V, SERVO5.+5V, SERVO6.+5V
  N3: Componente1.0, SERVO1.Signal
  N4: Componente1.1, SERVO2.Signal
  N5: Componente1.4, SERVO3.Signal
  N6: Componente1.5, SERVO4.Signal
  N7: Componente1.8, SERVO5.Signal
  N8: Componente1.9, SERVO6.Signal

custom parts:
  NodeMCU V3.0: ESP8266 based NodeMCU
  16-Channel 12-bit PCA9685 PWM/Servo Driver: The Adafruit 16-Channel 12-bit PWM/Servo Driver will drive up to 16 servos over I2C with only 2 pins. The on-board PCA9685 PWM controller will drive all 16 channels simultaneously with no additional processing overhead. What's more, you can chain up to 62 of them to control up to 992 servos - all with the same 2 pins
  Tower Pro SG90 servo: Original file by John De Cristofaro http://www.adafruit.com/products/1449 Adafruit Feedback Servo (Small) Edited by: e-radionica.com 28/9/2015
